# Fritzing sketch Schematic (saved by Fritzing 1.0.2b)
breadboards: 1

parts:
  U1 = Adafruit Feather M0 Adalogger [part_number="Adafruit #2796"]
  U2 = Adafruit 128x64 OLED FeatherWing [part_number="Adafruit #4650"]
  U3 = Adafruit FeatherWing Proto [part_number="Adafruit #2884"]
  LED1 = LEDs [mpn=IR333-A package=led10mm]
  LED2 = LEDs [mpn=XLUR12D mn=SunLED package=led10mm]
  Q3 = LTR-301 [mpn=ALS-PT204-6C/L177 mn="Everlight Electronics Co Ltd" package=ltr-301]
  Q4 = LTR-301 [mpn=ALS-PT204-6C/L177 mn="Everlight Electronics Co Ltd" package=ltr-301]
  R1 = Resistor [tolerance=±5% power=0.25W resistance=47 package=THT]
  R2 = Resistor [tolerance=±5% power=0.25W resistance=100 package=THT]
  R4 = Resistor [tolerance=±5% power=0.25W resistance=10M package=THT]
  Q2 = LTR-301 [mpn=1540031NC6090 mn="Würth Elektronik" package=ltr-301]
  C2 = Ceramic Capacitor [capacitance=1nF voltage=50V package="200 mil [THT, multilayer]"]
  C1 = Ceramic Capacitor [capacitance=1nF voltage=50V package="200 mil [THT, multilayer]"]
  R3 = Resistor [tolerance=±5% power=0.25W resistance=300k package=THT]
  Q1 = LTR-301 [mpn=1540031NC6090 mn="Würth Elektronik" package=ltr-301]
  R5 = Resistor [tolerance=±5% power=0.25W resistance=10M package=THT]
  R6 = Resistor [tolerance=±5% power=0.25W resistance=10M package=THT]
  R7 = Resistor [tolerance=±5% power=0.25W resistance=10M package=THT]
  R10 = Resistor [tolerance=±5% power=0.25W resistance=10M package=THT]
  R8 = Resistor [tolerance=±5% power=0.25W resistance=10M package=THT]
  R9 = Resistor [tolerance=±5% power=0.25W resistance=10M package=THT]
  R21 = Resistor [tolerance=±5% power=0.25W resistance=10M package=THT]
  R20 = Resistor [tolerance=±5% power=0.25W resistance=10M package=THT]
  R11 = Resistor [tolerance=±5% power=0.25W resistance=10M package=THT]
  R12 = Resistor [tolerance=±5% power=0.25W resistance=10M package=THT]
  R16 = Resistor [tolerance=±5% power=0.25W resistance=10M package=THT]
  R13 = Resistor [tolerance=±5% power=0.25W resistance=10M package=THT]
  R18 = Resistor [tolerance=±5% power=0.25W resistance=10M package=THT]
  R19 = Resistor [tolerance=±5% power=0.25W resistance=10M package=THT]
  R17 = Resistor [tolerance=±5% power=0.25W resistance=10M package=THT]
  R14 = Resistor [tolerance=±5% power=0.25W resistance=10M package=THT]
  R15 = Resistor [tolerance=±5% power=0.25W resistance=10M package=THT]
  C3 = Ceramic Capacitor [capacitance=1nF voltage=50V package="200 mil [THT, multilayer]"]
  C4 = Ceramic Capacitor [capacitance=1nF voltage=50V package="200 mil [THT, multilayer]"]

nets:
  GND: U1.GND, U2.GND, U3.GND
  N1: U1.A4, U3.E
  N2: U1.A3, U3.D
  N3: U1.A2, U3.C
  N4: U1.A1, U3.B, Q3.C, R10.Pin_1, C3.1
  +3V3: U1.+3V3, U2.3.3V, U3.3V, R4.Pin_0, R3.Pin_0, R5.Pin_1, R21.Pin_1
  N5: U1.!RESET, U2.!RESET
  N6: U1.D12, U3.M, R2.Pin_0
  N7: U1.D11, U3.L, R1.Pin_0
  N8: U1.D9, U2.J
  N9: U1.D6, U2.I
  N10: U1.D5, U2.H
  N11: U1.SCL, U2.SCL
  N12: U1.SDA, U2.SDA
  N13: U3.G, LED1.C, LED2.C, Q3.E, Q4.E, Q2.E, C2.0, C1.0, Q1.E, C3.0, C4.0
  N14: LED1.A, R2.Pin_1
  N15: LED2.A, R1.Pin_1
  N16: Q4.C, R11.Pin_1, C4.1
  N17: R4.Pin_1, Q2.C, C2.1
  N18: C1.1, R3.Pin_1, Q1.C
  N19: R5.Pin_0, R6.Pin_1
  N20: R6.Pin_0, R7.Pin_1
  N21: R7.Pin_0, R8.Pin_0
  N22: R10.Pin_0, R9.Pin_1
  N23: R8.Pin_1, R9.Pin_0
  N24: R21.Pin_0, R20.Pin_1
  N25: R20.Pin_0, R19.Pin_1
  N26: R11.Pin_0, R12.Pin_1
  N27: R12.Pin_0, R13.Pin_1
  N28: R16.Pin_0, R17.Pin_0
  N29: R16.Pin_1, R15.Pin_0
  N30: R13.Pin_0, R14.Pin_1
  N31: R18.Pin_0, R17.Pin_1
  N32: R18.Pin_1, R19.Pin_0
  N33: R14.Pin_0, R15.Pin_1

custom parts:
  Adafruit Feather M0 Adalogger: This is the Adafruit Feather M0 Adalogger - our take on an 'all-in-one' Cortex M0 datalogger (or data-reader) with built in USB and battery charging. Its an Adafruit Feather M0 with a microSD holder ready to rock! We have other boards in the Feather family, check'em out here At the Feather M0's heart is an ATSAMD21G18 ARM Cortex M0 processor, clocked at 48 MHz and at 3.3V logic, the same one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
  Adafruit 128x64 OLED FeatherWing: A Feather board without ambition is a Feather board without FeatherWings! This is the FeatherWing 128x64 OLED: it adds a gorgeous 128x64 monochrome OLED plus 3 user buttons to any Feather main board. Using our Feather Stacking Headers or Feather Female Headers you can connect a FeatherWing on top of your Feather board and let the board take flight! These displays are small, only about 1.3"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
  Adafruit FeatherWing Proto: This is the FeatherWing Proto - a prototyping add-on for all Feather boards. Using our Feather Stacking Headers or Feather Female Headers you can connect a FeatherWing on top or bottom of your Feather board and let the board take flight! This has a duplicate breakout for each pin on a Feather, as well as a bunch of plain grid proto holes. For GND and 3.3V, we give you a strip of connected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
